// Logisim project LC-3-v2.circ as structural Verilog: 16 circuits, main circuit main
// RES
module main (
  input  Reset,
  output out_2,
  output out_3,
  output out_4,
  output [2:0] out_5,
  output out_6,
  output out_7,
  output out_8,
  output [15:0] out_9,
  output [15:0] out_10,
  output [15:0] out_11,
  output [15:0] out_12,
  output [15:0] out_13,
  output [15:0] out_14,
  output [15:0] out_15,
  output [15:0] out_16,
  output [15:0] out_17,
  output halt,
  output [15:0] out_19,
  output [15:0] out_20,
  output [15:0] out_21,
  output [15:0] out_22
);

  wire decodeir_1_writereg, getcst_1_usecst, or16_1_out_2, or16_2_out_2, ramctrl_1_memload,
       ramctrl_1_memstore;
  wire [15:0] alu_1_output, getcst_1_cst, RegIN, registres_1_out_sr1, registres_1_out_sr2;

  BiClock biclock_1 (.reset(Reset), .signal0(out_2), .signal1(out_3));
  RegPC regpc_1 (
    .H(out_3), .PC(out_9), .Reset(Reset), .IR(out_10), .R(registres_1_out_sr1), .TestNZP(out_5), .Jump(out_4));
  // Probe on out_9
  // Probe on out_11
  GetAddr getaddr_1 (.PC(out_9), .BaseR(registres_1_out_sr1), .IR(out_10), .Addr(out_11), .Fetch(out_2));
  // Probe on out_12
  LED led_1 (.in(out_6));
  RamCtrl ramctrl_1 (
    .Store(out_7), .Fetch(out_2), .Exec(out_3), .Load(out_6), .MemStore(ramctrl_1_memstore),
    .MemLoad(ramctrl_1_memload));
  LED led_2 (.in(out_7));
  // Probe on out_13
  RAM #(.addrWidth(16), .dataWidth(16), .bus("separate")) ram_1 (
    .addr(out_11), .din(out_12), .data(out_13), .str(ramctrl_1_memstore), .clk(ramctrl_1_memstore),
    .ld(ramctrl_1_memload));  // open: sel, clr
  Register #(.width(16), .trigger("falling")) RegIR (.D(out_13), .Q(out_10), .clk(out_2));  // open: en, clr
  DecodeIR decodeir_1 (.IR(out_10), .Jump(out_4), .Load(out_6), .Store(out_7), .WriteReg(decodeir_1_writereg));
  // Probe on out_10[11:9]
  // Probe on out_10[8:6]
  // Probe on out_10[2:0]
  // Probe on getcst_1_cst
  GetCst getcst_1 (.IR(out_10), .Cst(getcst_1_cst), .UseCst(getcst_1_usecst));
  // Probe on out_10[15:14]
  and and_1 (out_8, decodeir_1_writereg, out_3);
  Registres registres_1 (
    .SR1(out_10[8:6]), .IN(RegIN), .SR2(out_10[2:0]), .WriteReg(out_8), .DR_SR(out_10[11:9]),
    .OUT_SR1(registres_1_out_sr1), .OUT_SR2(registres_1_out_sr2), .OUT_SR(out_12), .R0(out_14), .R1(out_15),
    .R2(out_16), .R3(out_17), .R4(out_19), .R5(out_20), .R6(out_21), .R7(out_22));
  // Probe on registres_1_out_sr1
  ALU alu_1 (
    .UseCst(getcst_1_usecst), .e2(out_10[15:14]), .Input1(registres_1_out_sr1), .Input2(registres_1_out_sr2),
    .Cst(getcst_1_cst), .Output(alu_1_output));
  // Probe on registres_1_out_sr2
  // Probe on alu_1_output
  NZP nzp_1 (.RES(RegIN), .NZP(out_5), .IR(out_10), .WriteReg(out_8));
  Or16 or16_1 (.in_1(out_10), .out_2(or16_1_out_2));
  Or16 or16_2 (.in_1(out_9), .out_2(or16_2_out_2));
  // Probe on out_14
  // Probe on out_15
  // Probe on out_16
  // Probe on out_17
  // Probe on out_19
  // Probe on out_20
  // Probe on out_21
  // Probe on out_22
  // Probe on out_5
  and and_2 (halt, ~or16_1_out_2, or16_2_out_2);  // AND_Gate
  WriteVal writeval_1 (.Load(out_6), .ALURes(alu_1_output), .MemOUT(out_13), .IR(out_10), .PC(out_9), .RegIN(RegIN));

  // Other names for the same wires on the sheet: Addr[15:0] = out_11; Condition[2:0] = out_5; Exec = out_3;
  //   Fetch = out_2; IR[15:0] = out_10; JumpInstr = out_4; Load = out_6; MemIN[15:0] = out_12; MemOUT[15:0] = out_13;
  //   PC[15:0] = out_9; R0[15:0] = out_14; R1[15:0] = out_15; R2[15:0] = out_16; R3[15:0] = out_17; R4[15:0] = out_19;
  //   R5[15:0] = out_20; R6[15:0] = out_21; R7[15:0] = out_22; Store = out_7; WriteReg = out_8

  // Notes on the sheet:
  //   R
  //   IR
  //   R
  //   IR
  //   RAM
  //   Traces (NE PAS MODIFIER)______________________________________________________________________________________________________
  //   GetOp
  //   Arret des traces au 1er NOP
endmodule

module ALU (
  input  [15:0] Input1,
  input  [15:0] Input2,
  input  [15:0] Cst,
  input  UseCst,
  input  [1:0] e2,
  output [15:0] Output
);

  wire [15:0] adder_1_out, and_1_out, multiplexer_1_out, not_1_out, scan_1_out_3;

  Multiplexer #(.width(16), .enable("false")) multiplexer_1 (
    .in0(Input2), .in1(Cst), .out(multiplexer_1_out), .sel(UseCst));
  Adder #(.width(16)) adder_1 (.a(multiplexer_1_out), .b(Input1), .out(adder_1_out));  // open: cin, cout
  assign and_1_out = Input1 & multiplexer_1_out;  // AND_Gate and_1, 16 bits wide
  Multiplexer #(.select(2), .width(16), .enable("false")) multiplexer_2 (
    .in0(adder_1_out), .in1(and_1_out), .in2(not_1_out), .in3(scan_1_out_3), .out(Output), .sel(e2));
  assign not_1_out = ~Input1;  // NOT_Gate not_1, 16 bits wide
  Scan scan_1 (.SR1(Input1), .out_3(scan_1_out_3), .SR2(multiplexer_1_out));
endmodule

module BiClock (
  input  reset,
  output signal0,
  output signal1
);

  wire and_1_out, horloge_out, not_1_out, register_1_q;

  Clock horloge (.out(horloge_out));
  not not_1 (not_1_out, register_1_q);
  Register #(.width(1), .trigger("falling")) register_1 (
    .D(not_1_out), .Q(register_1_q), .clk(horloge_out), .clr(reset));  // open: en
  and and_1 (and_1_out, horloge_out, ~reset);  // AND_Gate
  and and_2 (signal0, ~register_1_q, and_1_out);  // AND_Gate
  and and_3 (signal1, register_1_q, and_1_out);

  // Notes on the sheet:
  //   Ce module divise une horloge en deux sous-horloges alternées
  //   Chronogrammes :
  //   horloge: 0101010101 signal0: 0100010001 signal1: 000100010
  //   registre 1-bit
  //   Enable
  //   select : 0 / 1
endmodule

module DecodeIR (
  input  [15:0] IR,
  output Load,
  output Store,
  output Jump,
  output WriteReg
);

  wire and_1_out, and_2_out, and_4_out, and_6_out, and_7_out, nand_1_out, not_1_out, not_2_out, not_3_out,
       not_4_out, not_5_out, not_6_out, not_7_out;

  and and_1 (and_1_out, IR[12], IR[13], IR[14], IR[15]);
  and and_2 (and_2_out, IR[12], not_1_out);
  not not_1 (not_1_out, IR[13]);
  not not_2 (not_2_out, IR[12]);
  and and_3 (Load, not_2_out, IR[13]);
  and and_4 (and_4_out, IR[12], IR[13]);
  nand nand_1 (nand_1_out, IR[14], IR[15]);
  not not_3 (not_3_out, IR[12]);
  not not_4 (not_4_out, IR[13]);
  not not_5 (not_5_out, IR[12]);
  not not_6 (not_6_out, IR[13]);
  not not_7 (not_7_out, IR[15]);
  and and_5 (Store, and_4_out, nand_1_out);
  and and_6 (and_6_out, not_3_out, not_4_out);
  and and_7 (and_7_out, not_5_out, not_6_out, IR[14], not_7_out);
  or or_1 (Jump, and_1_out, and_6_out);
  or or_2 (WriteReg, and_2_out, Load, and_1_out, and_7_out);
  // Probe on and_2_out

  // Notes on the sheet:
  //   Types d'instructions
  //   TRAP
  //   ADD, AND, NOT, SCAN
  //   LD, LDR, LDI, LEA
  //   ST, STR, STI
  //   BR, JSR, RTI, JMP
  //   JSR
endmodule

module GetAddr (
  input  [15:0] IR,
  input  Fetch,
  input  [15:0] PC,
  input  [15:0] BaseR,
  output [15:0] Addr
);

  wire or_1_out;
  wire [15:0] adder_1_out, adder_2_out, multiplexer_1_out, offset6_1_off6, offset9_1_off9;

  Offset9 offset9_1 (.IR(IR), .Off9(offset9_1_off9));
  Offset6 offset6_1 (.IR(IR), .Off6(offset6_1_off6));
  Adder #(.width(16)) adder_1 (.a(offset6_1_off6), .b(BaseR), .out(adder_1_out));  // open: cin, cout
  Adder #(.width(16)) adder_2 (.a(offset9_1_off9), .b(PC), .out(adder_2_out), .cin(1'b1));  // open: cout
  Multiplexer #(.width(16), .disabled(0), .enable("false")) multiplexer_1 (
    .in0(adder_2_out), .in1(adder_1_out), .out(multiplexer_1_out), .sel(IR[14]));
  or or_1 (or_1_out, ~IR[13], Fetch);  // OR_Gate
  Multiplexer #(.width(16), .disabled(0), .enable("false")) multiplexer_2 (
    .in0(multiplexer_1_out), .in1(PC), .out(Addr), .sel(or_1_out));

  // Notes on the sheet:
  //   PC+SEXT(Offset6)
  //   b14: label or BaseR?
  //   PC+SEXT(Offset9)
  //   b13: Load ou Store?
  //   Pourquoi ?
endmodule

module GetCst (
  input  [15:0] IR,
  output [15:0] Cst,
  output UseCst
);

  assign Cst = {{11{IR[4]}}, IR[4:0]};  // Bit_Extender bit_extender_1

  assign UseCst = IR[5];
endmodule

module NZP (
  input  [15:0] RES,
  input  [15:0] IR,
  input  WriteReg,
  output [2:0] NZP
);

  wire not_1_out, not_2_out, not_3_out, or_1_out, or_2_out, xor_1_out;
  wire [1:0] and_1_out;

  or or_1 (or_1_out, RES[0], RES[1], RES[2], RES[3], RES[4], RES[5], RES[6], RES[7], RES[8], RES[9], RES[10], RES[11], RES[12], RES[13], RES[14]);
  and and_1 (and_1_out[0], or_1_out, not_1_out);
  not not_1 (not_1_out, RES[15]);
  not not_2 (not_2_out, or_1_out);
  not not_3 (not_3_out, RES[15]);
  xor xor_1 (xor_1_out, IR[12], IR[13]);
  and and_2 (and_1_out[1], not_2_out, not_3_out);
  Multiplexer #(.width(3), .enable("false")) multiplexer_1 (
    .in0(NZP), .in1({RES[15], and_1_out}), .out(NZP), .sel(or_2_out));
  or or_2 (or_2_out, xor_1_out, WriteReg);

  // Notes on the sheet:
  //   (Resultat du calcul courant)
  //   (Instruction courante)
  //   si 1, instruction doit actualiser NZP
  //   Valeur actuelle du registre d'état NZP
endmodule

// Off6
module Offset6 (
  input  [15:0] IR,
  output [15:0] Off6
);

  assign Off6 = {{10{IR[5]}}, IR[5:0]};  // Bit_Extender bit_extender_1
endmodule

// Off9
module Offset9 (
  input  [15:0] IR,
  output [15:0] Off9
);

  assign Off9 = {{7{IR[8]}}, IR[8:0]};  // Bit_Extender bit_extender_1
endmodule

module Or16 (
  input  [15:0] in_1,
  output out_2
);

  wire [1:0] or_2_out;
  wire [7:0] or_1_out;

  assign or_1_out = in_1[7:0] | in_1[15:8];  // OR_Gate or_1, 8 bits wide
  assign or_2_out = or_1_out[1:0] | or_1_out[3:2] | or_1_out[5:4] | or_1_out[7:6];  // OR_Gate or_2, 2 bits wide
  or or_3 (out_2, or_2_out[0], or_2_out[1]);
endmodule

module RamCtrl (
  input  Exec,
  input  Fetch,
  input  Load,
  input  Store,
  output MemLoad,
  output MemStore
);

  wire and_1_out;

  and and_1 (and_1_out, Exec, Load);
  and and_2 (MemStore, Exec, Store);
  or or_1 (MemLoad, Fetch, and_1_out);
endmodule

module Registres (
  input  [2:0] SR1,
  input  [15:0] IN,
  input  [2:0] SR2,
  input  WriteReg,
  input  [2:0] DR_SR,
  output [15:0] R0,
  output [15:0] OUT_SR1,
  output [15:0] R1,
  output [15:0] R2,
  output [15:0] R3,
  output [15:0] OUT_SR2,
  output [15:0] R4,
  output [15:0] R5,
  output [15:0] OUT_SR,
  output [15:0] R6,
  output [15:0] R7
);

  wire decoder_1_out0, decoder_1_out1, decoder_1_out2, decoder_1_out3, decoder_1_out4, decoder_1_out5,
       decoder_1_out6, decoder_1_out7;

  Decoder #(.select(3), .disabled(0)) decoder_1 (
    .out0(decoder_1_out0), .out1(decoder_1_out1), .out2(decoder_1_out2), .out3(decoder_1_out3),
    .out4(decoder_1_out4), .out5(decoder_1_out5), .out6(decoder_1_out6), .out7(decoder_1_out7), .sel(DR_SR),
    .en(WriteReg));
  Register #(.width(16), .trigger("falling")) u_R0 (.D(IN), .Q(R0), .clk(decoder_1_out0));  // open: en, clr
  Register #(.width(16), .trigger("falling")) u_R1 (.D(IN), .Q(R1), .clk(decoder_1_out1));  // open: en, clr
  Register #(.width(16), .trigger("falling")) u_R2 (.D(IN), .Q(R2), .clk(decoder_1_out2));  // open: en, clr
  Register #(.width(16), .trigger("falling")) u_R3 (.D(IN), .Q(R3), .clk(decoder_1_out3));  // open: en, clr
  Register #(.width(16), .trigger("falling")) u_R4 (.D(IN), .Q(R4), .clk(decoder_1_out4));  // open: en, clr
  Register #(.width(16), .trigger("falling")) u_R5 (.D(IN), .Q(R5), .clk(decoder_1_out5));  // open: en, clr
  Register #(.width(16), .trigger("falling")) u_R6 (.D(IN), .Q(R6), .clk(decoder_1_out6));  // open: en, clr
  Register #(.width(16), .trigger("falling")) u_R7 (.D(IN), .Q(R7), .clk(decoder_1_out7));  // open: en, clr
  Multiplexer #(.select(3), .width(16), .enable("false")) multiplexer_1 (
    .in0(R0), .in1(R1), .in2(R2), .in3(R3), .in4(R4), .in5(R5), .in6(R6), .in7(R7), .out(OUT_SR1), .sel(SR1));
  Multiplexer #(.select(3), .width(16), .enable("false")) multiplexer_2 (
    .in0(R0), .in1(R1), .in2(R2), .in3(R3), .in4(R4), .in5(R5), .in6(R6), .in7(R7), .out(OUT_SR2), .sel(SR2));
  Multiplexer #(.select(3), .width(16), .enable("false")) multiplexer_3 (
    .in0(R0), .in1(R1), .in2(R2), .in3(R3), .in4(R4), .in5(R5), .in6(R6), .in7(R7), .out(OUT_SR), .sel(DR_SR));
endmodule

module RegPC (
  input  [15:0] IR,
  input  [15:0] R,
  input  H,
  input  Reset,
  input  Jump,
  input  [2:0] TestNZP,
  output [15:0] PC
);

  wire and_1_out, JMP_out, JSR_out, JSRR_out, N_out, not_1_out, not_2_out, not_3_out, or_1_out, or_2_out,
       or_3_out, P_out, Z_out;
  wire [15:0] adder_1_out, adder_2_out, multiplexer_1_out, multiplexer_2_out, multiplexer_3_out,
       offset9_1_off9, offset11_1_sextoff11;

  not not_1 (not_1_out, IR[15]);
  Offset9 offset9_1 (.IR(IR), .Off9(offset9_1_off9));
  Offset11 offset11_1 (.IR(IR), .SEXTOff11(offset11_1_sextoff11));
  and JSR (JSR_out, IR[14], not_1_out, Jump);
  and JMP (JMP_out, IR[14], Jump, IR[15]);
  or or_1 (or_1_out, IR[12], IR[13], IR[14], IR[15]);
  Adder #(.width(16)) adder_1 (.a(PC), .b(16'h1), .out(adder_1_out));  // open: cin, cout
  Multiplexer #(.width(16), .disabled(0), .enable("false")) multiplexer_1 (
    .in0(offset9_1_off9), .in1(offset11_1_sextoff11), .out(multiplexer_1_out), .sel(JSR_out));
  not not_2 (not_2_out, IR[11]);
  not not_3 (not_3_out, or_1_out);
  and N (N_out, TestNZP[2], IR[11]);
  and Z (Z_out, IR[10], TestNZP[1]);
  and P (P_out, IR[9], TestNZP[0]);
  Adder #(.width(16)) adder_2 (.a(adder_1_out), .b(multiplexer_1_out), .out(adder_2_out));  // open: cin, cout
  and JSRR (JSRR_out, not_2_out, JSR_out);
  Multiplexer #(.width(16), .disabled(0), .enable("false")) multiplexer_2 (
    .in0(adder_2_out), .in1(R), .out(multiplexer_2_out), .sel(or_2_out));
  or or_2 (or_2_out, JSRR_out, JMP_out);
  or or_3 (or_3_out, N_out, Z_out, P_out);
  Multiplexer #(.width(16), .enable("false")) multiplexer_3 (
    .in0(adder_1_out), .in1(multiplexer_2_out), .out(multiplexer_3_out), .sel(and_1_out));
  and and_1 (and_1_out, Jump, not_3_out, or_3_out);
  Register #(.width(16), .trigger("falling")) u_PC (.D(multiplexer_3_out), .Q(PC), .clk(H), .clr(Reset));  // open: en

  // Notes on the sheet:
  //   pour BR
  //   pour JSR
  //   JSR ssi JMP et 14 et not 15
  //   PC <- PC + 1
  //   BaseR
  //   PC+Off
  //   pas saut
  //   saut
  //   BaseR ssi JMP ou JSRR
  //   saut ssi JMP et (BR =>TestNZP)
endmodule

module Offset11 (
  output [15:0] SEXTOff11,
  output [15:0] IR
);

  assign SEXTOff11 = {{5{1'b0}}, IR[10:0]};  // Bit_Extender bit_extender_1
endmodule

module WriteVal (
  input  [15:0] ALURes,
  input  [15:0] MemOUT,
  input  Load,
  input  [15:0] PC,
  input  [15:0] IR,
  output [15:0] RegIN
);

  wire JSR, LEA, or_1_out;
  wire [15:0] multiplexer_1_out, multiplexer_2_out, offset9_1_off9;

  Offset9 offset9_1 (.IR(PC), .Off9(offset9_1_off9));
  Multiplexer #(.width(16), .enable("false")) multiplexer_1 (
    .in0(ALURes), .in1(MemOUT), .out(multiplexer_1_out), .sel(Load));
  Multiplexer #(.width(16), .enable("false")) multiplexer_2 (
    .in0(PC), .in1(offset9_1_off9), .out(multiplexer_2_out), .sel(LEA));
  and and_1 (LEA, ~IR[12], IR[13], IR[14], IR[15]);  // AND_Gate
  and and_2 (JSR, ~IR[12], ~IR[13], IR[14], ~IR[15]);  // AND_Gate
  or or_1 (or_1_out, LEA, JSR);
  Multiplexer #(.width(16), .enable("false")) multiplexer_3 (
    .in0(multiplexer_1_out), .in1(multiplexer_2_out), .out(RegIN), .sel(or_1_out));

  // Notes on the sheet:
  //   RegIN = si JSR alors PC sinon si LEA alors PC+SEXT(Offset9) sinon si Load alors MemOUT sinon ALURes  
endmodule

module Scan (
  input  [15:0] SR1,
  input  [15:0] SR2,
  output [15:0] out_3
);

  wire [14:0] and_1_out;

  xor xor_1 (out_3[14], out_3[15], and_1_out[14]);
  xor xor_2 (out_3[13], out_3[14], and_1_out[13]);
  xor xor_3 (out_3[12], out_3[13], and_1_out[12]);
  assign {out_3[15], and_1_out} = SR1 & SR2;  // AND_Gate and_1, 16 bits wide
  xor xor_4 (out_3[11], out_3[12], and_1_out[11]);
  xor xor_5 (out_3[10], out_3[11], and_1_out[10]);
  xor xor_6 (out_3[9], out_3[10], and_1_out[9]);
  xor xor_7 (out_3[8], out_3[9], and_1_out[8]);
  xor xor_8 (out_3[7], out_3[8], and_1_out[7]);
  xor xor_9 (out_3[6], out_3[7], and_1_out[6]);
  xor xor_10 (out_3[5], out_3[6], and_1_out[5]);
  xor xor_11 (out_3[4], out_3[5], and_1_out[4]);
  xor xor_12 (out_3[3], out_3[4], and_1_out[3]);
  xor xor_13 (out_3[2], out_3[3], and_1_out[2]);
  xor xor_14 (out_3[1], out_3[2], and_1_out[1]);
  xor xor_15 (out_3[0], out_3[1], and_1_out[0]);
endmodule
